# Fritzing sketch ejer1 (saved by Fritzing 0.9.3b)
breadboards: 1

parts:
  Componente1 = Arduino Uno (Rev3)
  S1 = Pushbutton [package="[THT]"]
  LED1 = LED - 5mm [color="Red (633nm)" package="5 mm [THT]"]
  R1 = Resistor [tolerance=±5% resistance=330 package=THT]
  R2 = Resistor [tolerance=±5% resistance=1k package=THT]

nets:
  N1: Componente1.D9_PWM, LED1.anode
  N2: Componente1.D7, S1.Pin_3, S1.Pin_4, R2.Pin_0
  N3: Componente1.5V, R2.Pin_1
  N4: Componente1.GND, S1.Pin_1, S1.Pin_2, R1.Pin_1
  N5: LED1.cathode, R1.Pin_0
