# Fritzing sketch ejer2 (saved by Fritzing 0.9.3b)
breadboards: 1

parts:
  Componente1 = Arduino Uno (Rev3)
  J1 = Piezo Speaker
  S1 = Pushbutton [package="[THT]"]
  S2 = Pushbutton [package="[THT]"]
  LED1 = LED - 5mm [color="Red (633nm)" package="5 mm [THT]"]
  LED2 = LED - 5mm [color="Red (633nm)" package="5 mm [THT]"]
  R2 = Resistor [tolerance=±5% resistance=220 package=THT]
  R3 = Resistor [tolerance=±5% resistance=220 package=THT]

nets:
  N1: Componente1.D8, R3.Pin_1
  N2: Componente1.D11_PWM/MOSI, R2.Pin_1
  N3: Componente1.D13/SCK, J1.pin2
  N4: Componente1.GND, J1.pin1, S1.Pin_3, S1.Pin_4, S2.Pin_3, S2.Pin_4
  N5: Componente1.D2, S1.Pin_1, S1.Pin_2
  N6: Componente1.D5_PWM, S2.Pin_1, S2.Pin_2
  N7: LED1.cathode, LED2.cathode
  N8: LED1.anode, R3.Pin_0
  N9: LED2.anode, R2.Pin_0
